# Fritzing sketch 2-strip RGB LED schematic (saved by Fritzing 0.9.2b)
breadboards: 1

parts:
  mega = Arduino Mega 2560 (Rev3)
  NeoPixel_RGB_LED_strip_1 = mystery part, 4 pins [chip_label=NeoPixel]
  NeoPixel_RGB_LED_strip_2 = mystery part, 4 pins [chip_label=NeoPixel]
  DC_Power_Source = DC Power [voltage=9V]
  DC_Power_Source_2 = DC Power [voltage=5V]
  Capacitor = Electrolytic Capacitor [capacitance=4.7mF package="1010 [SMD, electrolytic]"]
  toggle_switch = SWITCH-MOMENTARY-2 [package=tactile-switch-1101ne]
  R1 = Resistor [tolerance=±5% resistance=220 package=THT]
  R2 = Resistor [tolerance=±5% resistance=220 package=THT]
  toggle_switch2 = SWITCH-MOMENTARY-2 [package=tactile-switch-1101ne]

nets:
  N1: mega.GND, NeoPixel_RGB_LED_strip_1.pin4, NeoPixel_RGB_LED_strip_2.pin4, DC_Power_Source.V-, DC_Power_Source_2.V-, Capacitor.-
  N2: mega.D9_PWM, R1.Pin_0
  N3: mega.VIN, toggle_switch2.2
  N4: mega.D3_PWM, R2.Pin_0
  N5: NeoPixel_RGB_LED_strip_1.pin1, NeoPixel_RGB_LED_strip_2.pin1, Capacitor.+, toggle_switch.1
  N6: NeoPixel_RGB_LED_strip_1.pin2, R2.Pin_1
  N7: NeoPixel_RGB_LED_strip_2.pin2, R1.Pin_1
  N8: DC_Power_Source.V+, toggle_switch2.1
  N9: DC_Power_Source_2.V+, toggle_switch.2

notes:
  Sparkfun Spectrum Shield
